// Logisim project TP78_EN2.circ as structural Verilog: 8 circuits, main circuit main
module main (
);

  // KeyPad keypad_1: pin names not known
  // FSM_Entity #(.content("state_machine example @[50,50,800,500]{\n	in A[3]   @[50,100,44,15];\n	out X[4]   @[807,140,43,15];\n	codeWidth = 2;\n	reset = S0;\n	\n	state S0[\"01\"]:\n	 	@[297,181,30,30]\n		set X=\"0001\";  @[297,181,30,30]	\n		goto S3  when (A==\"000\")   @[346,269,68,21]; \n		goto S1  when default   @[432,151,50,21]; \n	state S1[\"10\"]:\n	 	@[470,186,30,30]\n		set X=\"0010\";  @[470,186,30,30]	\n		goto S0  when (A==\"000\")   @[399,230,68,21]; \n		goto S2  when default   @[533,276,50,21]; \n	state S2[\"00\"]:\n	 	@[471,339,30,30]\n		set X={\"00\",A[0:1],\"1\"};  @[471,339,30,30]	\n		goto S1  when (A[2:1]==\"11\")   @[557,250,90,21]; \n		goto S3  when default   @[392,398,50,21]; \n	state S3[\"11\"]:\n	 	@[287,325,30,30]\n		set X=\"1000\";  @[287,325,30,30]	\n		goto S2  when (A==\"000\")   @[388,313,68,21]; \n		goto S0  when default   @[248,278,50,21]; \n}")) fsm_entity_1: pin names not known
endmodule

module keypad_FSM (
  input  Clk,
  input  Rst,
  input  En,
  input  Lhit,
  input  Ack,
  output [3:0] C,
  output Load,
  output Req
);

  // FSM_Entity #(.content("state_machine KeyPAd @[50,49,800,500]{\n	in Lhit[1]   @[50,164,24,15];Ack[1]   @[50,237,26,15];\n	out C[4]   @[815,140,35,15];load[1]   @[823,202,27,15];req[1]   @[827,262,23,15];\n	codeWidth = 4;\n	reset = S0;\n	\n	state S0[\"0000\"]:\n	 	@[88,135,30,30]\n		set C=\"0000\";load=\"0\";req=\"0\";  @[88,135,30,30]	\n		goto S1  when default   @[212,201,41,22]; \n	state S1[\"0001\"]:\n	 	@[281,97,30,30]\n		set C=\"0001\";  @[281,97,30,30]	\n		goto S5  when Lhit   @[297,200,24,22]; \n		goto S2  when default   @[362,169,41,22]; \n	state S2[\"0010\"]:\n	 	@[440,122,30,30]\n		set C=\"0010\";  @[440,122,30,30]	\n		goto S6  when Lhit   @[434,212,24,22]; \n		goto S3  when default   @[503,186,41,22]; \n	state S3[\"0011\"]:\n	 	@[545,122,30,30]\n		set C=\"0100\";  @[545,122,30,30]	\n		goto S7  when Lhit   @[574,204,24,22]; \n		goto S4  when default   @[643,174,41,22]; \n	state S4[\"0100\"]:\n	 	@[688,91,30,30]\n		set C=\"1000\";  @[688,91,30,30]	\n		goto S8  when Lhit   @[726,198,24,22]; \n		goto S1  when default   @[532,95,41,22]; \n	state S5[\"0101\"]:\n	 	@[238,240,30,30]\n		set C=\"0001\";load=\"1\";req=\"1\";  @[238,240,30,30]	\n		goto S9  when default   @[282,320,41,22]; \n	state S6[\"0110\"]:\n	 	@[393,248,30,30]\n		set C=\"0010\";load=\"1\";req=\"1\";  @[393,248,30,30]	\n		goto S10  when default   @[419,323,41,22]; \n	state S7[\"0111\"]:\n	 	@[563,242,30,30]\n		set C=\"0100\";load=\"1\";req=\"1\";  @[563,242,30,30]	\n		goto S11  when default   @[570,325,41,22]; \n	state S8[\"1000\"]:\n	 	@[722,245,30,30]\n		set C=\"1000\";load=\"1\";req=\"1\";  @[722,245,30,30]	\n		goto S12  when default   @[729,328,41,22]; \n	state S9[\"1001\"]:\n	 	@[267,362,30,30]\n		set C=\"0001\";load=\"0\";req=\"1\";  @[267,362,30,30]	\n		goto S13  when (Ack.(/Lhit))   @[303,447,67,22]; \n	state S10[\"1010\"]:\n	 	@[410,370,30,30]\n		set C=\"0010\";load=\"0\";req=\"1\";  @[410,370,30,30]	\n		goto S13  when (Ack.(/Lhit))   @[410,442,67,22]; \n	state S11[\"1011\"]:\n	 	@[577,365,30,30]\n		set C=\"0100\";load=\"0\";req=\"1\";  @[577,365,30,30]	\n		goto S13  when (Ack.(/Lhit))   @[535,444,67,22]; \n	state S13[\"1101\"]:\n	 	@[438,485,30,30]\n		set load=\"0\";req=\"0\";  @[438,485,30,30]	\n		goto S0  when (/Ack)   @[198,465,38,22]; \n	state S12[\"1100\"]:\n	 	@[722,374,30,30]\n		set C=\"1000\";load=\"0\";req=\"1\";  @[722,374,30,30]	\n		goto S13  when (Ack.(/Lhit))   @[683,446,67,22]; \n}")) FSM: pin names not known; wires that end beside it: Clk, Rst, En, Lhit, Ack, C, Load, Req
endmodule

module Test_KEyPAd (
  input  CLK,
  input  RST,
  input  En,
  input  ACK,
  output [3:0] out_5,
  output Req,
  output [3:0] C,
  output [3:0] KEY
);

  wire detec_lhit, kry_load;
  wire [3:0] dec_k, kp_p5;

  // KeyPad kp: pin names not known; wires that end beside it: C[0], C[1], C[2], C[3], kp_p5[0], kp_p5[1], kp_p5[2], kp_p5[3]
  DetecTouche detec (.L0(kp_p5[0]), .L1(kp_p5[1]), .L2(kp_p5[2]), .L3(kp_p5[3]), .Lhit(detec_lhit));
  keypad_FSM kry (.Clk(CLK), .Rst(RST), .En(En), .Lhit(detec_lhit), .Ack(ACK), .C(C), .Load(kry_load), .Req(Req));
  Decodeur_keypad_a319796e dec (.C(C), .L(kp_p5), .K(dec_k));
  Memorisation memo (.K(dec_k), .H(CLK), .Load(kry_load), .Rst(RST), .key(KEY));

  assign out_5 = C;
endmodule

module DetecTouche (
  input  L0,
  input  L1,
  input  L2,
  input  L3,
  output Lhit
);

  or or_1 (Lhit, L0, L1, L2, L3);
endmodule

module Memorisation (
  input  [3:0] K,
  input  H,
  input  Load,
  input  Rst,
  output [3:0] key
);

  Register #(.width(4)) register_1 (.D(K), .en(Load), .clk(H), .Q(key), .clr(Rst));
endmodule

module Decodeur_keypad_a319796e (
  input  [3:0] C,
  input  [3:0] L,
  output [3:0] K
);

  wire and_1_out, and_2_out, and_3_out, and_4_out, and_5_out, and_6_out, and_7_out, and_8_out, and_9_out,
       and_10_out, not_1_out, not_2_out, not_3_out, not_4_out, not_5_out, not_6_out, not_7_out, not_8_out,
       not_9_out, not_10_out, not_11_out, not_12_out, not_13_out, not_14_out;

  not not_1 (not_1_out, C[0]);
  not not_2 (not_2_out, C[1]);
  not not_3 (not_3_out, L[0]);
  and and_1 (and_1_out, C[0], L[2]);
  not not_4 (not_4_out, C[1]);
  not not_5 (not_5_out, C[0]);
  not not_6 (not_6_out, L[3]);
  not not_7 (not_7_out, L[2]);
  not not_8 (not_8_out, C[0]);
  not not_9 (not_9_out, C[3]);
  not not_10 (not_10_out, C[1]);
  not not_11 (not_11_out, C[1]);
  not not_12 (not_12_out, L[3]);
  not not_13 (not_13_out, L[1]);
  not not_14 (not_14_out, L[1]);
  and and_2 (and_2_out, not_1_out, L[2]);
  and and_3 (and_3_out, not_2_out, L[3], not_3_out);
  or or_1 (K[2], L[1], and_1_out, C[3]);
  and and_4 (and_4_out, not_4_out, not_5_out, not_6_out, not_7_out);
  and and_5 (and_5_out, not_8_out, L[0]);
  and and_6 (and_6_out, not_9_out, not_10_out, L[3]);
  and and_7 (and_7_out, C[0], L[2]);
  and and_8 (and_8_out, not_11_out, not_12_out, not_13_out);
  and and_9 (and_9_out, C[1], L[1]);
  and and_10 (and_10_out, C[2], not_14_out);
  or or_2 (K[3], and_2_out, and_3_out, C[3]);
  or or_3 (K[1], and_4_out, and_5_out, and_6_out, and_7_out);
  or or_4 (K[0], and_8_out, and_9_out, and_10_out);
endmodule

module keypad_interface (
  input  e
);

  wire ACK, clk, REQ;
  wire [3:0] C, decoder_key, L;

  // KeyPad kp: pin names not known; wires that end beside it: C[0], C[1], C[2], C[3], L[0], L[1], L[2], L[3]
  Clock u_clk (.out(clk));
  // FSM_Entity #(.content("state_machine example @[50,50,800,500]{\n	in REQ[1]   @[50,100,32,15];\n	out ACK[1]   @[820,139,30,15];\n	codeWidth = 2;\n	reset = S0;\n	\n	state S0[\"01\"]:\n	 	@[266,166,30,30]\n		set ACK=\"0\";  @[266,166,30,30]	\n		goto S1  when REQ   @[429,149,32,22]; \n	state S1[\"10\"]:\n	 	@[563,180,30,30]\n		set ACK=\"1\";  @[563,180,30,30]	\n		goto S0  when (/REQ)   @[397,231,44,22]; \n}")) FSM1: pin names not known; wires that end beside it: clk, e, 1'b1, REQ, ACK
  keypad_decoder decoder (.CLK(clk), .RST(e), .L(L), .ACK(ACK), .Req(REQ), .C(C), .KEY(decoder_key));
  // Bin_to_7_Segment_decoder bin_to_7_segment_decoder_1: pin names not known; wires that end beside it: decoder_key
  _7_Segment_Display u_7_segment_display_1 ();  // open: g, f, a, b, e, d, c, dp

  // Other names for the same wires on the sheet: reset = e
endmodule

module keypad_decoder (
  input  CLK,
  input  RST,
  input  [3:0] L,
  input  ACK,
  output Req,
  output [3:0] C,
  output [3:0] KEY
);

  wire detec_lhit, kry_load;
  wire [3:0] dec_k;

  DetecTouche detec (.L0(L[0]), .L1(L[1]), .L2(L[2]), .L3(L[3]), .Lhit(detec_lhit));
  keypad_FSM kry (.Clk(CLK), .Rst(RST), .En(1'b1), .Lhit(detec_lhit), .Ack(ACK), .C(C), .Load(kry_load), .Req(Req));
  Decodeur_keypad_a319796e dec (.C(C), .L(L), .K(dec_k));
  Memorisation memo (.K(dec_k), .H(CLK), .Load(kry_load), .Rst(RST), .key(KEY));
endmodule
