// Logisim project TP78_calculatrice_SEN2_v3.circ as structural Verilog: 1 circuit, main circuit calculatrice
module calculatrice (
);

  wire ACK, affiche_q, and_1_out, bcd_to_7_segment_decoder_1_p10, bcd_to_7_segment_decoder_3_p1,
       bcd_to_7_segment_decoder_4_p1, binary_to_bcd_converter_1_p2, clk, isDigit, or_1_out, REQ, rst, SelA,
       SelB, SelIn1, Selnxt, showA, showB, WEA, WEB, WENxt;
  wire [1:0] Op;
  wire [3:0] key, KeyPad_1_p1, KeyPad_1_p5, multiplexer_1_out, nxt_op;
  wire [15:0] A_q, B_q, bit_extender_1_out, multiplexer_2_out, multiplexer_3_out, multiplexer_4_out,
       multiplexer_5_out, ual_calc_1_r;

  Clock u_clk (.out(clk));
  Button u_rst (.out(rst));
  // KeyPad KeyPad_1: pin names not known; wires that end beside it: KeyPad_1_p1[0], KeyPad_1_p1[1], KeyPad_1_p1[2], KeyPad_1_p1[3], KeyPad_1_p5[0], KeyPad_1_p5[1], KeyPad_1_p5[2], KeyPad_1_p5[3]
  // Probe on key
  // Probe on nxt_op
  // Probe on isDigit
  // Probe on Op
  Multiplexer #(.width(4), .enable("false")) multiplexer_1 (
    .in0(key), .in1(4'b1111), .out(multiplexer_1_out), .sel(Selnxt));
  Comparator #(.width(4), .mode("unsigned")) comparator_1 (.a(4'b1010), .b(key), .gt(isDigit));  // open: eq, lt
  keypad_decoder keypad_decoder_1 (
    .CLK(clk), .RST(rst), .L(KeyPad_1_p5), .ACK(ACK), .Req(REQ), .C(KeyPad_1_p1), .KEY(key));
  and and_1 (and_1_out, showA, ~showB);  // AND_Gate
  or or_1 (or_1_out, showA, showB);
  Register #(.width(4)) u_nxt_op (.D(multiplexer_1_out), .en(WENxt), .clk(clk), .Q(nxt_op), .clr(rst));
  Register #(.width(1)) affiche (.D(and_1_out), .en(or_1_out), .clk(clk), .Q(affiche_q), .clr(rst));
  _7_Segment_Display hex_key ();  // open: g, f, a, b, e, d, c, dp
  // Bin_to_7_Segment_decoder bin_to_7_segment_decoder_1: pin names not known; wires that end beside it: key
  Multiplexer #(.width(16), .enable("false")) multiplexer_2 (
    .in0(ual_calc_1_r), .in1({16{1'b0}}), .out(multiplexer_2_out), .sel(SelA));
  Multiplexer #(.width(16), .enable("false")) multiplexer_3 (
    .in0({16{1'b0}}), .in1(ual_calc_1_r), .out(multiplexer_3_out), .sel(SelB));
  Register #(.width(16)) A (.D(multiplexer_2_out), .en(WEA), .clk(clk), .Q(A_q), .clr(rst));
  Register #(.width(16)) B (.D(multiplexer_3_out), .en(WEB), .clk(clk), .Q(B_q), .clr(rst));
  // FSM_Entity #(.content("state_machine calculatrice_UC @[50,50,1000,800]{\n	in REQ[1]   @[50,199,32,15];key[4]   @[50,236,47,15];isDigit[1]   @[50,280,41,15];NxtOp[4]   @[50,327,62,15];\n	out ACK[1]   @[1020,99,30,15];showA[1]   @[1007,129,43,15];showB[1]   @[1006,166,44,15];SelIn1[1]   @[1009,203,41,15];WEA[1]   @[1018,245,32,15];WEB[1]   @[1017,279,33,15];SelB[1]   @[1018,335,32,15];SelA[1]   @[1019,368,31,15];Op[2]   @[1005,413,45,15];WENxt[1]   @[1008,445,42,15];Selnxt[1]   @[1011,482,39,15];\n	codeWidth = 4;\n	reset = INIT;\n	\n	state INIT[\"0000\"]:\n	 	@[111,109,30,30]\n		set WENxt=\"1\";Selnxt=\"1\";  @[111,109,30,30]	\n		goto S1  when default   @[264,101,43,22]; \n	state S1[\"0001\"]:\n	 	@[364,101,30,30]\n		set ACK=\"0\";  @[364,101,30,30]	\n		goto S9  when REQ   @[439,129,32,22]; \n	state S2[\"0010\"]:\n	 	@[390,237,30,30]\n		set SelIn1=\"1\";SelA=\"0\";Op=\"11\";WEA=\"1\";showA=\"1\";  @[390,237,30,30]	\n		goto S3  when default   @[310,324,43,22]; \n	state S3[\"0011\"]:\n	 	@[168,291,30,30]\n		set ACK=\"1\";  @[168,291,30,30]	\n		goto S1  when (/REQ)   @[303,232,43,22]; \n	state S4[\"0100\"]:\n	 	@[655,84,30,30]\n		set ACK=\"0\";  @[655,84,30,30]	\n		goto S5  when (NxtOp==\"1111\")   @[606,195,97,22]; \n		goto S6  when (NxtOp==\"1110\")   @[709,222,97,22]; \n		goto S7  when (NxtOp==\"1101\")   @[825,186,97,22]; \n		goto S8  when (NxtOp==\"1010\")   @[882,123,97,22]; \n		goto S10  when (NxtOp==\"1100\")   @[533,226,97,22]; \n	state S5[\"0101\"]:\n	 	@[478,331,30,30]\n		set WEB=\"1\";WEA=\"1\";SelA=\"1\";SelB=\"1\";Op=\"00\";showB=\"1\";Selnxt=\"0\";WENxt=\"1\";SelIn1=\"0\";  @[478,331,30,30]	\n		goto S3  when default   @[380,473,43,22]; \n	state S6[\"0110\"]:\n	 	@[608,329,30,30]\n		set WEA=\"1\";WEB=\"1\";SelA=\"1\";SelB=\"1\";Op=\"01\";showB=\"1\";Selnxt=\"0\";WENxt=\"1\";SelIn1=\"0\";  @[608,329,30,30]	\n		goto S3  when default   @[393,530,43,22]; \n	state S7[\"0111\"]:\n	 	@[734,330,30,30]\n		set WEA=\"1\";WEB=\"1\";SelA=\"1\";SelB=\"1\";Op=\"10\";showB=\"1\";Selnxt=\"0\";WENxt=\"1\";SelIn1=\"0\";  @[734,330,30,30]	\n		goto S3  when default   @[403,581,43,22]; \n	state S8[\"1000\"]:\n	 	@[856,329,30,30]\n		set WEA=\"1\";WEB=\"1\";SelA=\"1\";SelB=\"0\";showB=\"1\";Selnxt=\"1\";WENxt=\"1\";SelIn1=\"0\";  @[856,329,30,30]	\n		goto S3  when default   @[400,662,43,22]; \n	state S9[\"1001\"]:\n	 	@[474,126,30,30]\n		goto S2  when (REQ.isDigit)   @[449,205,78,22]; \n		goto S4  when (REQ.(/isDigit))   @[533,134,89,22]; \n	state S10[\"1010\"]:\n	 	@[382,332,30,30]\n		set WEA=\"1\";WEB=\"1\";SelB=\"1\";SelA=\"1\";showB=\"1\";WENxt=\"1\";  @[382,332,30,30]	\n		goto S3  when default   @[381,427,43,22]; \n}")) a_completer: pin names not known; wires that end beside it: clk, rst, 1'b1, REQ, key, isDigit, nxt_op, ACK, showA
  Multiplexer #(.width(16), .enable("false")) multiplexer_4 (
    .in0(B_q), .in1(A_q), .out(multiplexer_4_out), .sel(affiche_q));
  assign bit_extender_1_out = {{12{1'b0}}, key};  // Bit_Extender bit_extender_1
  _7_Segment_Display Seg3 ();  // open: g, f, a, b, e, d, c, dp
  // BCD_to_7_Segment_decoder bcd_to_7_segment_decoder_1: pin names not known; wires that end beside it: showB, SelIn1, WEA, WEB, SelB, SelA, Op, WENxt, Selnxt, bcd_to_7_segment_decoder_1_p10
  _7_Segment_Display Seg2 ();  // open: g, f, a, b, e, d, c, dp
  // BCD_to_7_Segment_decoder bcd_to_7_segment_decoder_2: pin names not known
  // Binary_to_BCD_converter #(.binvalue(12)) binary_to_bcd_converter_1: pin names not known; wires that end beside it: multiplexer_4_out[11:0], binary_to_bcd_converter_1_p2, binary_to_bcd_converter_1_p2, bcd_to_7_segment_decoder_1_p10
  // Probe on Op
  // Probe on multiplexer_5_out
  Multiplexer #(.width(16), .enable("false")) multiplexer_5 (
    .in0(B_q), .in1(bit_extender_1_out), .out(multiplexer_5_out), .sel(SelIn1));
  // BCD_to_7_Segment_decoder bcd_to_7_segment_decoder_3: pin names not known; wires that end beside it: bcd_to_7_segment_decoder_3_p1, bcd_to_7_segment_decoder_3_p1
  _7_Segment_Display Seg1 ();  // open: g, f, a, b, e, d, c, dp
  // BCD_to_7_Segment_decoder bcd_to_7_segment_decoder_4: pin names not known; wires that end beside it: bcd_to_7_segment_decoder_4_p1, bcd_to_7_segment_decoder_4_p1
  _7_Segment_Display Seg0 ();  // open: g, f, a, b, e, d, c, dp
  UAL_calc ual_calc_1 (.Op(Op), .In0(A_q), .In1(multiplexer_5_out), .R(ual_calc_1_r));
  // Probe on ual_calc_1_r

  // Notes on the sheet:
  //   Interface Keypad
  //   UnitÃ© de calcul
  //   UnitÃ© de contrÃ´le
  //   UAL_calc
endmodule
