// Logisim project ual_calc.circ as structural Verilog: 1 circuit, main circuit UAL_calc
module UAL_calc (
  input  [1:0] Op,
  input  [15:0] In0,
  input  [15:0] In1,
  output [15:0] R
);

  wire [15:0] adder_1_out, adder_2_out, multiplexer_1_out, multiplier_1_out, subtractor_1_out;

  Multiplexer #(.width(16), .enable("false")) multiplexer_1 (
    .in0(In1), .in1(16'ha), .out(multiplexer_1_out), .sel(Op[0]));
  Adder #(.width(16)) adder_1 (.a(In0), .b(In1), .out(adder_1_out));  // open: cin, cout
  Subtractor #(.width(16)) subtractor_1 (.a(In1), .b(In0), .out(subtractor_1_out));  // open: bin, bout
  Multiplier #(.width(16)) multiplier_1 (.a(In0), .b(multiplexer_1_out), .out(multiplier_1_out));  // open: cin, cout
  Adder #(.width(16)) adder_2 (.a(multiplier_1_out), .b(In1), .out(adder_2_out));  // open: cin, cout
  Multiplexer #(.select(2), .width(16), .enable("false")) multiplexer_2 (
    .in0(adder_1_out), .in1(subtractor_1_out), .in2(multiplier_1_out), .in3(adder_2_out), .out(R), .sel(Op));
endmodule
