// Logisim project unite_de_calcul.circ as structural Verilog: 1 circuit, main circuit unite_de_calcul
module unite_de_calcul (
  input  WEA,
  input  WEB,
  input  WENxt,
  input  SELA,
  input  SELB,
  input  Selnxt,
  input  [1:0] OP,
  input  SELIn1,
  input  showA,
  input  showB,
  input  clk,
  input  rst,
  input  [3:0] key,
  output [3:0] out_14,
  output [1:0] out_15,
  output [15:0] out_16,
  output [15:0] out_17
);

  wire affiche_q, and_1_out, bcd_to_7_segment_decoder_2_p1, bcd_to_7_segment_decoder_3_p1,
       bcd_to_7_segment_decoder_4_p1, binary_to_bcd_converter_1_p2, isDigit, or_1_out;
  wire [3:0] multiplexer_1_out;
  wire [15:0] B_q, bit_extender_1_out, multiplexer_2_out, multiplexer_3_out, multiplexer_4_out, ual_calc_1_r;

  Multiplexer #(.width(4), .enable("false")) multiplexer_1 (
    .in0(key), .in1(4'b1111), .out(multiplexer_1_out), .sel(Selnxt));
  Comparator #(.width(4), .mode("unsigned")) comparator_1 (.a(4'b1010), .b(key), .gt(isDigit));  // open: eq, lt
  and and_1 (and_1_out, showA, ~showB);  // AND_Gate
  or or_1 (or_1_out, showA, showB);
  Register #(.width(4)) nxt_op (.D(multiplexer_1_out), .en(WENxt), .clk(clk), .Q(out_14), .clr(rst));
  Register #(.width(1)) affiche (.D(and_1_out), .en(or_1_out), .clk(clk), .Q(affiche_q), .clr(rst));
  Multiplexer #(.width(16), .enable("false")) multiplexer_2 (
    .in0(ual_calc_1_r), .in1({16{1'b0}}), .out(multiplexer_2_out), .sel(SELA));
  Multiplexer #(.width(16), .enable("false")) multiplexer_3 (
    .in0({16{1'b0}}), .in1(ual_calc_1_r), .out(multiplexer_3_out), .sel(SELB));
  Register #(.width(16)) A (.D(multiplexer_2_out), .en(WEA), .clk(clk), .Q(out_16), .clr(rst));
  Register #(.width(16)) B (.D(multiplexer_3_out), .en(WEB), .clk(clk), .Q(B_q), .clr(rst));
  Multiplexer #(.width(16), .enable("false")) multiplexer_4 (
    .in0(B_q), .in1(out_16), .out(multiplexer_4_out), .sel(affiche_q));
  assign bit_extender_1_out = {{12{1'b0}}, key};  // Bit_Extender bit_extender_1
  _7_Segment_Display Seg2 ();  // open: g, f, a, b, e, d, c, dp
  _7_Segment_Display Seg3 ();  // open: g, f, a, b, e, d, c, dp
  // BCD_to_7_Segment_decoder bcd_to_7_segment_decoder_1: pin names not known
  // BCD_to_7_Segment_decoder bcd_to_7_segment_decoder_2: pin names not known; wires that end beside it: bcd_to_7_segment_decoder_2_p1
  // Binary_to_BCD_converter #(.binvalue(12)) binary_to_bcd_converter_1: pin names not known; wires that end beside it: multiplexer_4_out[11:0], binary_to_bcd_converter_1_p2, binary_to_bcd_converter_1_p2, bcd_to_7_segment_decoder_2_p1
  Multiplexer #(.width(16), .enable("false")) multiplexer_5 (
    .in0(B_q), .in1(bit_extender_1_out), .out(out_17), .sel(SELIn1));
  _7_Segment_Display Seg1 ();  // open: g, f, a, b, e, d, c, dp
  // BCD_to_7_Segment_decoder bcd_to_7_segment_decoder_3: pin names not known; wires that end beside it: bcd_to_7_segment_decoder_3_p1, bcd_to_7_segment_decoder_3_p1
  // BCD_to_7_Segment_decoder bcd_to_7_segment_decoder_4: pin names not known; wires that end beside it: bcd_to_7_segment_decoder_4_p1, bcd_to_7_segment_decoder_4_p1
  _7_Segment_Display Seg0 ();  // open: g, f, a, b, e, d, c, dp
  UAL_calc ual_calc_1 (.Op(OP), .In0(out_16), .In1(out_17), .R(ual_calc_1_r));
  // Probe on ual_calc_1_r

  assign out_15 = OP;

  // Other names for the same wires on the sheet: nxt_op[3:0] = out_14

  // Notes on the sheet:
  //   Unité de calcul
endmodule
